# Fritzing sketch Synthesizer_Clock_Module_Fritzing_Files (saved by Fritzing 0.9.10b)
circuit board: 7.19755cm x 4.12889cm
breadboards: 1

parts:
  MCU_Arduino_Nano = Arduino Nano (Rev3.0)
  ENCODER1 = KY-040
  Button = Square Pushbutton
  D1 = Diode [package=diode-1n4148]
  Signal_out1 = female pin header, 2 pins [form="♀ (female)"]
  R1 = Resistor [tolerance=±5% power=0.25 resistance=100000 package=THT]
  12V_Input = female pin header, 2 pins [form="♀ (female)"]
  R2 = Resistor [tolerance=±5% power=0.25 resistance=100000 package=THT]
  Signal_out2 = female pin header, 2 pins [form="♀ (female)"]
  D2 = Diode [package=diode-1n4148]
  64_x_32_OLED_SSD1306 = Grove OLED 128x96
  IC1 = Dual Op-Amp [package=dip08]
  VIN = female pin header, 2 pins [form="♀ (female)"]
  I2C_Test = female pin header, 2 pins [form="♀ (female)"]

nets:
  GND: MCU_Arduino_Nano.GND, ENCODER1.GND, Button.leg0, 64_x_32_OLED_SSD1306.GND, VIN.pin2
  N1: MCU_Arduino_Nano.D3, Button.leg1
  N2: MCU_Arduino_Nano.D4, ENCODER1.SW
  N3: MCU_Arduino_Nano.D5, ENCODER1.DT
  N4: MCU_Arduino_Nano.D6, ENCODER1.CLK
  N5: MCU_Arduino_Nano.D12/MISO, D2.A
  N6: MCU_Arduino_Nano.VIN, VIN.pin1
  N7: MCU_Arduino_Nano.A5, 64_x_32_OLED_SSD1306.SCL, I2C_Test.pin1
  N8: MCU_Arduino_Nano.A4, 64_x_32_OLED_SSD1306.SDA, I2C_Test.pin2
  3V3: MCU_Arduino_Nano.3V3, ENCODER1.+, 64_x_32_OLED_SSD1306.VCC
  N9: MCU_Arduino_Nano.D13/SCK, D1.A
  N10: D1.C, R1.Pin_0, IC1.A_+IN
  N11: Signal_out1.pin1, Signal_out1.pin2, IC1.A_OUT, IC1.A_-IN
  N12: R1.Pin_1, 12V_Input.pin2, R2.Pin_1, IC1.A_V-
  N13: 12V_Input.pin1, IC1.A_V+
  N14: R2.Pin_0, D2.C, IC1.B_+IN
  N15: Signal_out2.pin1, Signal_out2.pin2, IC1.B_-IN, IC1.B_OUT

notes:
  JRC4558 seems to work, but the signal is inverted. Would be nice to find a circuit or part that can not be inverted from the input and output between 3V low and 12V high
  Synth Sequencer Clock Module, The goal of this circuit is to provide some clock signal through an arduino.  , 1.0.0
  Vcc
  GND
  Designed by Brandon Thibeaux
  Pin1
  SLC
  SDA

custom parts:
  KY-040: Rotary encoder with button
